# Fritzing sketch sketch_hw02 (saved by Fritzing 0.9.2b)
circuit board: 8.46667cm x 5.64444cm
breadboards: 2

parts:
  BeagleBone1 = BeagleBone Black
  R1 = Resistor [tolerance=±5% resistance=220 package=THT]
  LED1 = LED - 5mm [color="Red (633nm)" package="5 mm [THT]"]
  LED2 = LED - 5mm [color="Red (633nm)" package="5 mm [THT]"]
  R2 = Resistor [tolerance=±5% resistance=220 package=THT]
  LED3 = LED - 5mm [color="Red (633nm)" package="5 mm [THT]"]
  R3 = Resistor [tolerance=±5% resistance=220 package=THT]
  LED4 = LED - 5mm [color="Red (633nm)" package="5 mm [THT]"]
  R4 = Resistor [tolerance=±5% resistance=220 package=THT]
  S1 = Pushbutton [package="[THT]"]
  S2 = Pushbutton [package="[THT]"]
  S3 = Pushbutton [package="[THT]"]
  S4 = Pushbutton [package="[THT]"]

nets:
  N1: BeagleBone1.no_name_yet#1, LED1.cathode, LED2.cathode, LED3.cathode, LED3.anode, R3.Pin_0, LED4.cathode
  N2: BeagleBone1.no_name_yet#3, S1.Pin_1, S1.Pin_2, S2.Pin_1, S2.Pin_2, S3.Pin_1, S3.Pin_2, S4.Pin_1, S4.Pin_2
  N3: BeagleBone1.no_name_yet#12, R4.Pin_1
  N4: BeagleBone1.no_name_yet#15, R3.Pin_1
  N5: BeagleBone1.no_name_yet#23, R2.Pin_0
  N6: BeagleBone1.no_name_yet#25, R1.Pin_1
  N7: BeagleBone1.no_name_yet#108, S1.Pin_3, S1.Pin_4
  N8: BeagleBone1.no_name_yet#110, S2.Pin_3, S2.Pin_4
  N9: BeagleBone1.no_name_yet#112, S3.Pin_3, S3.Pin_4
  N10: BeagleBone1.no_name_yet#114, S4.Pin_3, S4.Pin_4
  N11: R1.Pin_0, LED1.anode
  N12: LED2.anode, R2.Pin_1
  N13: LED4.anode, R4.Pin_0

custom parts:
  BeagleBone Black: BeagleBone Black rev. A5B
