# Fritzing sketch Untitled Sketch (saved by Fritzing 0.9.2b)
breadboards: 1

parts:
  BeagleBone2 = BeagleBone Black
  Part1 = LSM303 Breakout Board - Tilt-Compensated Compass
  R1 = Resistor [tolerance=±5% resistance=220 package=THT]
  R2 = Resistor [tolerance=±5% resistance=220 package=THT]

nets:
  N1: BeagleBone2.no_name_yet#1, Part1.GND
  N2: BeagleBone2.no_name_yet#2, Part1.VCC, R1.Pin_0
  N3: BeagleBone2.no_name_yet#18, BeagleBone2.no_name_yet#19, Part1.INT2, R2.Pin_1
  N4: BeagleBone2.no_name_yet#20, Part1.INT1, R1.Pin_1

custom parts:
  BeagleBone Black: BeagleBone Black rev. A5B
